# Fritzing sketch MSS_Uno (saved by Fritzing 1.0.1rc)
breadboards: 1

parts:
  Part1 = Arduino Uno (Rev3)
  R1 = Resistor [tolerance=±5% power=0.25W resistance=220 package=THT]
  Speaker = Piezo Speaker
  LED_Addressible_Strip = mystery part, 3 pins [chip_label=LED]
  Power_Smoothing_Cap = Electrolytic Capacitor [capacitance=100µF voltage=35V package="200 mil [THT, electrolytic]"]
  LED_Overdraw_LED = smd LED [color="Red (633nm)" package="0603 [SMD]"]
  R2 = Resistor [tolerance=±5% power=0.25W resistance=330 package=THT]

nets:
  N1: Part1.GND, Speaker.pin1, LED_Addressible_Strip.pin1, Power_Smoothing_Cap.-, LED_Overdraw_LED.cathode
  N2: Part1.D2, R2.Pin_1
  N3: Part1.D3_PWM, Speaker.pin2
  N4: Part1.D4, R1.Pin_1
  N5: Part1.5V, LED_Addressible_Strip.pin3, Power_Smoothing_Cap.+
  N6: R1.Pin_0, LED_Overdraw_LED.anode
  N7: LED_Addressible_Strip.pin2, R2.Pin_0
